# Fritzing sketch dkdevre (saved by Fritzing 0.9.3b)
breadboards: 1

parts:
  T3_Vakfı1 = Generic shrouded header - 32 pins [package=THT]
  LCD2004-I2C1 = LCD2004-I2C

nets:
  N1: T3_Vakfı1.pin15, LCD2004-I2C1.VCC
  N2: T3_Vakfı1.pin16, LCD2004-I2C1.GND
  N3: T3_Vakfı1.pin20, LCD2004-I2C1.SCL
  N4: T3_Vakfı1.pin21, LCD2004-I2C1.SDA

notes:
  GND->GND
  VCC->5V
  SDA->SDA
  SCl->SCL

custom parts:
  Generic shrouded header - 32 pins: Ülkemizin mühendislik kaynakları kullanılarak geliştirilen Deneyap Kart; güçlü işlemcisi, dayanıklı tasarımı ve çok yönlü giriş/çıkış pinleri ile kullanıcılara Elektronik Programlama, Nesnelerin İnterneti (IoT) ve Yapay Zeka alanlarında başlangıç seviyesinden endüstriyel uygulamalara kadar her seviyede projeyi yapma imkanı sunuyor.
  LCD2004-I2C: A standard character display with 4x20 characters. Comes in many colors with LCM2004 IIC attached.
