# Fritzing sketch nanodevre (saved by Fritzing 0.9.3b)
breadboards: 1

parts:
  Parça1 = Arduino Nano (Rev3.0)
  LCD2004-I2C1 = LCD2004-I2C

nets:
  GND: Parça1.GND, LCD2004-I2C1.GND
  5V: Parça1.5V, LCD2004-I2C1.VCC
  N1: Parça1.A5, LCD2004-I2C1.SCL
  N2: Parça1.A4, LCD2004-I2C1.SDA

notes:
  GND->GND
  VCC->5V
  SDA->A4
  SCL->A5

custom parts:
  LCD2004-I2C: A standard character display with 4x20 characters. Comes in many colors with LCM2004 IIC attached.
